# Fritzing sketch s4d (saved by Fritzing 0.8.3b)
breadboards: 2

parts:
  Onderdeel1 = Arduino Uno (Rev3)
  U1 = POT [package=pot_alpha_rv16af-20]
  U2 = POT [package=pot_alpha_rv16af-20]
  LED1 = RGB LED (com. anode, rbg) [package="5 mm [THT]"]
  R1 = Resistor [package="2512 [SMD]"]
  R2 = Resistor [package="2512 [SMD]"]
  R3 = Resistor [package="2512 [SMD]"]
  S2 = Pushbutton [package="[THT]"]
  S3 = Pushbutton [package="[THT]"]
  S4 = Pushbutton [package="[THT]"]
  LED2 = RGB LED (com. anode, rbg) [package="5 mm [THT]"]
  J1 = Piezo Speaker
  R4 = Resistor [package="2512 [SMD]"]
  R5 = Resistor [package="2512 [SMD]"]
  R6 = Resistor [package="2512 [SMD]"]
  R7 = Resistor [tolerance=±20% resistance=100 package=THT]
  R8 = Resistor [tolerance=±20% resistance=100 package=THT]
  R9 = Resistor [tolerance=±20% resistance=100 package=THT]
  Onderdeel2 = Arduino Uno (Rev3)
  S5 = Pushbutton [package="[THT]"]
  S6 = Pushbutton [package="[THT]"]
  S7 = Pushbutton [package="[THT]"]
  U3 = POT [package=pot_alpha_rv16af-20]  # not connected
  U4 = POT [package=pot_alpha_rv16af-20]  # not connected
  LED3 = RGB LED (com. anode, rbg) [package="5 mm [THT]"]  # not connected
  LED4 = RGB LED (com. anode, rbg) [package="5 mm [THT]"]  # not connected

nets:
  N1: Onderdeel1.A0, U1.S
  N2: Onderdeel1.A1, U2.S
  N3: Onderdeel1.ICSP_MOSI, Onderdeel1.D11_PWM/MOSI, R4.Pin_0
  N4: Onderdeel1.GND, U1.E, LED1.blue_cathode, LED2.blue_cathode, R8.Pin_1, R9.Pin_1
  N5: Onderdeel1.D8, Onderdeel1.5V, U1.A, U2.A, U2.E, S2.Pin_1, S2.Pin_2, S3.Pin_1, S3.Pin_2, S4.Pin_1, S4.Pin_2
  N6: Onderdeel1.D9_PWM, R6.Pin_0
  N7: Onderdeel1.D10_PWM/SS, R5.Pin_0
  N8: Onderdeel1.D2, S4.Pin_3, S4.Pin_4, R9.Pin_0
  N9: Onderdeel1.D3_PWM, R2.Pin_0
  N10: Onderdeel1.D5_PWM, R3.Pin_0
  N11: Onderdeel1.D6_PWM, R1.Pin_0
  N12: Onderdeel1.D7, S3.Pin_3, S3.Pin_4, R8.Pin_0
  N13: LED1.red_cathode, R1.Pin_1
  N14: LED1.common_anode, R3.Pin_1
  N15: LED1.green_cathode, R2.Pin_1
  N16: S2.Pin_3, S2.Pin_4, R7.Pin_0
  N17: J1.pin2, Onderdeel2.D4
  N18: S5.Pin_1, S5.Pin_2
  N19: S5.Pin_3, S5.Pin_4
  N20: S6.Pin_1, S6.Pin_2
  N21: S6.Pin_3, S6.Pin_4
  N22: S7.Pin_1, S7.Pin_2
  N23: S7.Pin_3, S7.Pin_4

notes:
  Vooraanzicht
  Let op.
  De buzzer kon er niet in één keer bij. Deze is apart getekend.
  Alles moet op één bord.
  Het lange pootje bij de led is de tweede van links (in deze view).
  De led is hieronder getekend zoals de pootjes in het bord zitten.
  O
  | | | |
  | | |
  | |
  |
